// Logisim project ETFStudent.circ as structural Verilog: 13 circuits, main circuit REG32_LD
module REG32_LD (
  input  [31:0] I15__0,
  input  LD,
  input  mr,
  input  CLK,
  output [31:0] A15__0
);

  REG16_LD reg16_ld_1 (.I15__0(I15__0[31:16]), .LD(LD), .CLK(CLK), .A15__0(A15__0[31:16]), .mr(mr));
  REG16_LD reg16_ld_2 (.I15__0(I15__0[15:0]), .LD(LD), .CLK(CLK), .A15__0(A15__0[15:0]), .mr(mr));

  // Notes on the sheet:
  //   __
endmodule

module KMADR (
  input  immed,
  input  memdir,
  input  regdir,
  input  regindpom,
  output [3:0] Adr3__0
);

  assign Adr3__0 = immed ? 4'b0010 : 4'bz;  // Controlled_Buffer controlled_buffer_1
  assign Adr3__0 = memdir ? 4'b0100 : 4'bz;  // Controlled_Buffer controlled_buffer_2
  assign Adr3__0 = regdir ? 4'b0101 : 4'bz;  // Controlled_Buffer controlled_buffer_3
  assign Adr3__0 = regindpom ? 4'b0111 : 4'bz;  // Controlled_Buffer controlled_buffer_4
endmodule

module KMOPR (
  input  LD,
  input  ST,
  input  ADD,
  input  SUB,
  input  BLSS,
  input  JLEQ,
  input  JMP,
  input  JSR,
  input  RTS,
  input  RTI,
  input  HALT,
  output [5:0] Adr5__0
);

  assign Adr5__0 = LD ? 6'b000010 : 6'bz;  // Controlled_Buffer controlled_buffer_1
  assign Adr5__0 = ST ? 6'b000100 : 6'bz;  // Controlled_Buffer controlled_buffer_2
  assign Adr5__0 = ADD ? 6'b001010 : 6'bz;  // Controlled_Buffer controlled_buffer_3
  assign Adr5__0 = SUB ? 6'b001100 : 6'bz;  // Controlled_Buffer controlled_buffer_4
  assign Adr5__0 = BLSS ? 6'b001110 : 6'bz;  // Controlled_Buffer controlled_buffer_5
  assign Adr5__0 = JLEQ ? 6'b010000 : 6'bz;  // Controlled_Buffer controlled_buffer_6
  assign Adr5__0 = JMP ? 6'b010001 : 6'bz;  // Controlled_Buffer controlled_buffer_7
  assign Adr5__0 = JSR ? 6'b010010 : 6'bz;  // Controlled_Buffer controlled_buffer_8
  assign Adr5__0 = RTS ? 6'b010111 : 6'bz;  // Controlled_Buffer controlled_buffer_9
  assign Adr5__0 = RTI ? 6'b011110 : 6'bz;  // Controlled_Buffer controlled_buffer_10
  assign Adr5__0 = HALT ? 6'b100010 : 6'bz;  // Controlled_Buffer controlled_buffer_11
endmodule

module REG6_INC_LD (
  input  [5:0] I5__0,
  input  LD,
  input  INC,
  input  mr,
  input  CLK,
  output [5:0] A5__0
);

  wire reg2m_inc_ld_2_cout, reg2m_inc_ld_3_cout;

  REG2m_INC_LD reg2m_inc_ld_1 (
    .I1__0(I5__0[5:4]), .LD(LD), .Cin(reg2m_inc_ld_2_cout), .INC(INC), .CLK(CLK), .A1__0(A5__0[5:4]), .mr(mr));  // open: Cout
  REG2m_INC_LD reg2m_inc_ld_2 (
    .I1__0(I5__0[3:2]), .LD(LD), .Cin(reg2m_inc_ld_3_cout), .INC(INC), .CLK(CLK), .Cout(reg2m_inc_ld_2_cout),
    .A1__0(A5__0[3:2]), .mr(mr));
  REG2m_INC_LD reg2m_inc_ld_3 (
    .I1__0(I5__0[1:0]), .LD(LD), .Cin(INC), .INC(INC), .CLK(CLK), .Cout(reg2m_inc_ld_3_cout),
    .A1__0(A5__0[1:0]), .mr(mr));

  // Notes on the sheet:
  //   __
endmodule

module ROM_32x24 (
  input  [4:0] A4__0,
  input  CS,
  output [23:0] DOUT
);

  ROM #(.addrWidth(5), .dataWidth(24)) rom_1 (.addr(A4__0), .data(DOUT), .sel(CS));
endmodule

module GPR16x16 (
  input  [15:0] DI15__0,
  input  [3:0] A3__0,
  input  WR,
  input  CLK,
  output [15:0] DO15__0
);

  wire and_1_out, and_2_out, and_3_out, and_4_out, and_5_out, and_6_out, and_7_out, and_8_out, and_9_out,
       and_10_out, and_11_out, and_12_out, and_13_out, and_14_out, and_15_out, and_16_out, CS0, CS1, CS2,
       CS3, CS4, CS5, CS6, CS7, CS8, CS9, CS10, CS11, CS12, CS13, CS14, CS15;
  wire [15:0] reg16_ld_1_a15__0, reg16_ld_2_a15__0, reg16_ld_3_a15__0, reg16_ld_4_a15__0, reg16_ld_5_a15__0,
       reg16_ld_6_a15__0, reg16_ld_7_a15__0, reg16_ld_8_a15__0, reg16_ld_9_a15__0, reg16_ld_10_a15__0,
       reg16_ld_11_a15__0, reg16_ld_12_a15__0, reg16_ld_13_a15__0, reg16_ld_14_a15__0, reg16_ld_15_a15__0,
       reg16_ld_16_a15__0;

  DC4_16 dc4_16_1 (
    .En(1'b1), .X3__0(A3__0), .D0(CS0), .D1(CS1), .D2(CS2), .D3(CS3), .D4(CS4), .D5(CS5), .D6(CS6), .D7(CS7),
    .D8(CS8), .D9(CS9), .D10(CS10), .D11(CS11), .D12(CS12), .D13(CS13), .D14(CS14), .D15(CS15));
  REG16_LD reg16_ld_1 (.I15__0(DI15__0), .LD(and_1_out), .CLK(CLK), .A15__0(reg16_ld_1_a15__0));  // open: mr
  assign DO15__0 = CS0 ? reg16_ld_1_a15__0 : 16'bz;  // Controlled_Buffer controlled_buffer_1
  REG16_LD reg16_ld_2 (.I15__0(DI15__0), .LD(and_2_out), .CLK(CLK), .A15__0(reg16_ld_2_a15__0));  // open: mr
  assign DO15__0 = CS1 ? reg16_ld_2_a15__0 : 16'bz;  // Controlled_Buffer controlled_buffer_2
  REG16_LD reg16_ld_3 (.I15__0(DI15__0), .LD(and_3_out), .CLK(CLK), .A15__0(reg16_ld_3_a15__0));  // open: mr
  assign DO15__0 = CS2 ? reg16_ld_3_a15__0 : 16'bz;  // Controlled_Buffer controlled_buffer_3
  REG16_LD reg16_ld_4 (.I15__0(DI15__0), .LD(and_4_out), .CLK(CLK), .A15__0(reg16_ld_4_a15__0));  // open: mr
  assign DO15__0 = CS3 ? reg16_ld_4_a15__0 : 16'bz;  // Controlled_Buffer controlled_buffer_4
  and and_1 (and_1_out, CS0, WR);
  and and_2 (and_2_out, CS1, WR);
  and and_3 (and_3_out, CS2, WR);
  and and_4 (and_4_out, CS3, WR);
  REG16_LD reg16_ld_5 (.I15__0(DI15__0), .LD(and_5_out), .CLK(CLK), .A15__0(reg16_ld_5_a15__0));  // open: mr
  and and_5 (and_5_out, CS4, WR);
  assign DO15__0 = CS4 ? reg16_ld_5_a15__0 : 16'bz;  // Controlled_Buffer controlled_buffer_5
  REG16_LD reg16_ld_6 (.I15__0(DI15__0), .LD(and_6_out), .CLK(CLK), .A15__0(reg16_ld_6_a15__0));  // open: mr
  and and_6 (and_6_out, CS5, WR);
  assign DO15__0 = CS5 ? reg16_ld_6_a15__0 : 16'bz;  // Controlled_Buffer controlled_buffer_6
  and and_7 (and_7_out, CS6, WR);
  REG16_LD reg16_ld_7 (.I15__0(DI15__0), .LD(and_7_out), .CLK(CLK), .A15__0(reg16_ld_7_a15__0));  // open: mr
  assign DO15__0 = CS6 ? reg16_ld_7_a15__0 : 16'bz;  // Controlled_Buffer controlled_buffer_7
  REG16_LD reg16_ld_8 (.I15__0(DI15__0), .LD(and_8_out), .CLK(CLK), .A15__0(reg16_ld_8_a15__0));  // open: mr
  and and_8 (and_8_out, CS7, WR);
  assign DO15__0 = CS7 ? reg16_ld_8_a15__0 : 16'bz;  // Controlled_Buffer controlled_buffer_8
  and and_9 (and_9_out, CS8, WR);
  REG16_LD reg16_ld_9 (.I15__0(DI15__0), .LD(and_9_out), .CLK(CLK), .A15__0(reg16_ld_9_a15__0));  // open: mr
  assign DO15__0 = CS8 ? reg16_ld_9_a15__0 : 16'bz;  // Controlled_Buffer controlled_buffer_9
  REG16_LD reg16_ld_10 (.I15__0(DI15__0), .LD(and_10_out), .CLK(CLK), .A15__0(reg16_ld_10_a15__0));  // open: mr
  and and_10 (and_10_out, CS9, WR);
  assign DO15__0 = CS9 ? reg16_ld_10_a15__0 : 16'bz;  // Controlled_Buffer controlled_buffer_10
  and and_11 (and_11_out, CS10, WR);
  REG16_LD reg16_ld_11 (.I15__0(DI15__0), .LD(and_11_out), .CLK(CLK), .A15__0(reg16_ld_11_a15__0));  // open: mr
  assign DO15__0 = CS10 ? reg16_ld_11_a15__0 : 16'bz;  // Controlled_Buffer controlled_buffer_11
  and and_12 (and_12_out, CS11, WR);
  REG16_LD reg16_ld_12 (.I15__0(DI15__0), .LD(and_12_out), .CLK(CLK), .A15__0(reg16_ld_12_a15__0));  // open: mr
  assign DO15__0 = CS11 ? reg16_ld_12_a15__0 : 16'bz;  // Controlled_Buffer controlled_buffer_12
  REG16_LD reg16_ld_13 (.I15__0(DI15__0), .LD(and_13_out), .CLK(CLK), .A15__0(reg16_ld_13_a15__0));  // open: mr
  assign DO15__0 = CS12 ? reg16_ld_13_a15__0 : 16'bz;  // Controlled_Buffer controlled_buffer_13
  REG16_LD reg16_ld_14 (.I15__0(DI15__0), .LD(and_14_out), .CLK(CLK), .A15__0(reg16_ld_14_a15__0));  // open: mr
  assign DO15__0 = CS13 ? reg16_ld_14_a15__0 : 16'bz;  // Controlled_Buffer controlled_buffer_14
  REG16_LD reg16_ld_15 (.I15__0(DI15__0), .LD(and_15_out), .CLK(CLK), .A15__0(reg16_ld_15_a15__0));  // open: mr
  assign DO15__0 = CS14 ? reg16_ld_15_a15__0 : 16'bz;  // Controlled_Buffer controlled_buffer_15
  REG16_LD reg16_ld_16 (.I15__0(DI15__0), .LD(and_16_out), .CLK(CLK), .A15__0(reg16_ld_16_a15__0));  // open: mr
  assign DO15__0 = CS15 ? reg16_ld_16_a15__0 : 16'bz;  // Controlled_Buffer controlled_buffer_16
  and and_13 (and_13_out, CS12, WR);
  and and_14 (and_14_out, CS13, WR);
  and and_15 (and_15_out, CS14, WR);
  and and_16 (and_16_out, CS15, WR);

  // Other names for the same wires on the sheet: inREG[15:0] = DI15__0; outREG[15:0] = DO15__0
endmodule

module KMADRADDR (
  input  immed,
  input  memdir,
  input  memind,
  input  regind,
  input  preincr,
  input  postdecr,
  input  regdir,
  output [3:0] Adr3__0
);

  assign Adr3__0 = immed ? 4'b0010 : 4'bz;  // Controlled_Buffer controlled_buffer_1
  assign Adr3__0 = memdir ? 4'b0011 : 4'bz;  // Controlled_Buffer controlled_buffer_2
  assign Adr3__0 = memind ? 4'b0100 : 4'bz;  // Controlled_Buffer controlled_buffer_3
  assign Adr3__0 = regind ? 4'b1010 : 4'bz;  // Controlled_Buffer controlled_buffer_4
  assign Adr3__0 = preincr ? 4'b1011 : 4'bz;  // Controlled_Buffer controlled_buffer_5
  assign Adr3__0 = postdecr ? 4'b1101 : 4'bz;  // Controlled_Buffer controlled_buffer_6
  assign Adr3__0 = regdir ? 4'b1111 : 4'bz;  // Controlled_Buffer controlled_buffer_7
endmodule

module ROM_32x24_addr (
  input  [4:0] A4__0,
  input  CS,
  output [23:0] DOUT
);

  ROM #(.addrWidth(5), .dataWidth(24)) rom_1 (.addr(A4__0), .data(DOUT), .sel(CS));
endmodule

module ROM_EXEC (
  input  [7:0] A7__0,
  input  CS,
  output [23:0] DOUT51_26,
  output [27:0] DOUT25__0
);

  ROM #(.dataWidth(28)) rom_1 (.addr(A7__0), .data(DOUT25__0), .sel(CS));
  ROM #(.dataWidth(24)) rom_2 (.addr(A7__0), .data(DOUT51_26), .sel(CS));
endmodule

module KMDAR_EXEC (
  input  LD,
  input  ST,
  input  ADD,
  input  DEC,
  input  OR,
  input  STRFIND,
  input  BRANCH,
  input  JAPS,
  input  JMP,
  input  JSR,
  input  RTS,
  input  RTI,
  input  ROR,
  input  RORC,
  input  PUSHPSW,
  input  POPPSW,
  input  STIVTP,
  input  HALT,
  output [7:0] Adr7__0
);

  assign Adr7__0 = LD ? 8'h2 : 8'bz;  // Controlled_Buffer controlled_buffer_1
  assign Adr7__0 = ST ? 8'h4 : 8'bz;  // Controlled_Buffer controlled_buffer_2
  assign Adr7__0 = ADD ? 8'hb : 8'bz;  // Controlled_Buffer controlled_buffer_3
  assign Adr7__0 = DEC ? 8'hd : 8'bz;  // Controlled_Buffer controlled_buffer_4
  assign Adr7__0 = OR ? 8'hf : 8'bz;  // Controlled_Buffer controlled_buffer_5
  assign Adr7__0 = STRFIND ? 8'h11 : 8'bz;  // Controlled_Buffer controlled_buffer_6
  assign Adr7__0 = BRANCH ? 8'h19 : 8'bz;  // Controlled_Buffer controlled_buffer_7
  assign Adr7__0 = JAPS ? 8'h1b : 8'bz;  // Controlled_Buffer controlled_buffer_8
  assign Adr7__0 = JMP ? 8'h1c : 8'bz;  // Controlled_Buffer controlled_buffer_9
  assign Adr7__0 = JSR ? 8'h1d : 8'bz;  // Controlled_Buffer controlled_buffer_10
  assign Adr7__0 = RTS ? 8'h22 : 8'bz;  // Controlled_Buffer controlled_buffer_11
  assign Adr7__0 = RTI ? 8'h28 : 8'bz;  // Controlled_Buffer controlled_buffer_12
  assign Adr7__0 = ROR ? 8'h2e : 8'bz;  // Controlled_Buffer controlled_buffer_13
  assign Adr7__0 = RORC ? 8'h30 : 8'bz;  // Controlled_Buffer controlled_buffer_14
  assign Adr7__0 = PUSHPSW ? 8'h32 : 8'bz;  // Controlled_Buffer controlled_buffer_15
  assign Adr7__0 = POPPSW ? 8'h38 : 8'bz;  // Controlled_Buffer controlled_buffer_16
  assign Adr7__0 = STIVTP ? 8'h3e : 8'bz;  // Controlled_Buffer controlled_buffer_17
  assign Adr7__0 = HALT ? 8'h3f : 8'bz;  // Controlled_Buffer controlled_buffer_18
endmodule

module ROM32x26 (
  input  [4:0] A3__0,
  input  CS,
  output [25:0] DOUT
);

  ROM #(.addrWidth(5), .dataWidth(26)) rom_1 (.addr(A3__0), .data(DOUT), .sel(CS));
endmodule

module ROM256x52 (
  input  [7:0] A7__0,
  input  CS,
  output [31:0] DOUT59__28,
  output [27:0] DOUT27__0
);

  ROM #(.dataWidth(32)) rom_1 (.addr(A7__0), .data(DOUT59__28), .sel(CS));
  ROM #(.dataWidth(28)) rom_2 (.addr(A7__0), .data(DOUT27__0), .sel(CS));
endmodule

module KMADR_MODIF (
  input  LD,
  input  ST,
  input  ADD,
  input  DEC,
  input  OR,
  input  STRFIND,
  input  BRANCH,
  input  JAPS,
  input  JMP,
  input  JSR,
  input  RTS,
  input  RTI,
  input  ROR,
  input  RORC,
  input  PUSHPSW,
  input  POPPSW,
  input  STIVTP,
  input  HALT,
  input  MODIF,
  output [7:0] Adr7__0
);

  assign Adr7__0 = LD ? 8'h2 : 8'bz;  // Controlled_Buffer controlled_buffer_1
  assign Adr7__0 = ST ? 8'h4 : 8'bz;  // Controlled_Buffer controlled_buffer_2
  assign Adr7__0 = ADD ? 8'hb : 8'bz;  // Controlled_Buffer controlled_buffer_3
  assign Adr7__0 = DEC ? 8'hd : 8'bz;  // Controlled_Buffer controlled_buffer_4
  assign Adr7__0 = OR ? 8'hf : 8'bz;  // Controlled_Buffer controlled_buffer_5
  assign Adr7__0 = STRFIND ? 8'h11 : 8'bz;  // Controlled_Buffer controlled_buffer_6
  assign Adr7__0 = JAPS ? 8'h1b : 8'bz;  // Controlled_Buffer controlled_buffer_7
  assign Adr7__0 = BRANCH ? 8'h19 : 8'bz;  // Controlled_Buffer controlled_buffer_8
  assign Adr7__0 = JMP ? 8'h1c : 8'bz;  // Controlled_Buffer controlled_buffer_9
  assign Adr7__0 = RTS ? 8'h22 : 8'bz;  // Controlled_Buffer controlled_buffer_10
  assign Adr7__0 = JSR ? 8'h1d : 8'bz;  // Controlled_Buffer controlled_buffer_11
  assign Adr7__0 = RTI ? 8'h28 : 8'bz;  // Controlled_Buffer controlled_buffer_12
  assign Adr7__0 = ROR ? 8'h2e : 8'bz;  // Controlled_Buffer controlled_buffer_13
  assign Adr7__0 = RORC ? 8'h30 : 8'bz;  // Controlled_Buffer controlled_buffer_14
  assign Adr7__0 = PUSHPSW ? 8'h32 : 8'bz;  // Controlled_Buffer controlled_buffer_15
  assign Adr7__0 = POPPSW ? 8'h38 : 8'bz;  // Controlled_Buffer controlled_buffer_16
  assign Adr7__0 = STIVTP ? 8'h3e : 8'bz;  // Controlled_Buffer controlled_buffer_17
  assign Adr7__0 = HALT ? 8'h3f : 8'bz;  // Controlled_Buffer controlled_buffer_18
  assign Adr7__0 = MODIF ? {8{1'b1}} : 8'bz;  // Controlled_Buffer controlled_buffer_19
endmodule
