// Logisim project ORT2Project.circ as structural Verilog: 8 circuits, main circuit COMPUTER
module COMPUTER (
);

  wire BTN_INTR0_out, BTN_INTR1_out, BTN_INTR2_out, BTN_INTR3_out, BTN_RST_out, CLK, cpu_1_inta,
       pull_resistor_4_node, pull_resistor_6_node, ram_1_out_8, rst;
  wire [1:0] cpu_1_uext1__0;
  wire [3:0] interrupt_interface_4_1_intr3__0;
  wire [7:0] pull_resistor_2_node, ram_1_out_7;
  wire [15:0] pull_resistor_3_node;

  Button BTN_RST (.out(BTN_RST_out));
  Clock u_CLK (.out(CLK));
  RisingEdge risingedge_1 (.INPUT(BTN_RST_out), .CLK(CLK), .OUTPUT(rst));
  RAM ram_1 (
    .in_1(pull_resistor_3_node), .in_3(pull_resistor_2_node), .in_4(pull_resistor_4_node),
    .in_5(pull_resistor_6_node), .in_6(rst), .out_7(ram_1_out_7), .out_8(ram_1_out_8), .in_2(CLK));
  Pull_Resistor pull_resistor_1 (.node(ram_1_out_7));
  Pull_Resistor pull_resistor_2 (.node(pull_resistor_2_node));
  Pull_Resistor pull_resistor_3 (.node(pull_resistor_3_node));
  Pull_Resistor pull_resistor_4 (.node(pull_resistor_4_node));
  Pull_Resistor pull_resistor_5 (.node(ram_1_out_8));
  Pull_Resistor pull_resistor_6 (.node(pull_resistor_6_node));
  CPU cpu_1 (
    .in_1(rst), .in_3(ram_1_out_8), .in_4(ram_1_out_7), .ABUS(pull_resistor_3_node),
    .DOUTBUS(pull_resistor_2_node), .out_10(pull_resistor_4_node), .out_11(pull_resistor_6_node),
    .inta(cpu_1_inta), .intr3__0(interrupt_interface_4_1_intr3__0), .UEXT1__0(cpu_1_uext1__0), .CLK(CLK));
  INTERRUPT_INTERFACE_4 interrupt_interface_4_1 (
    .BTN_INTR0(BTN_INTR0_out), .BTN_INTR1(BTN_INTR1_out), .BTN_INTR2(BTN_INTR2_out),
    .BTN_INTR3(BTN_INTR3_out), .inta(cpu_1_inta), .UEXT1__0(cpu_1_uext1__0), .CLK(CLK),
    .intr3__0(interrupt_interface_4_1_intr3__0));
  Button BTN_INTR3 (.out(BTN_INTR3_out));
  Button BTN_INTR2 (.out(BTN_INTR2_out));
  Button BTN_INTR1 (.out(BTN_INTR1_out));
  Button BTN_INTR0 (.out(BTN_INTR0_out));
endmodule

module CPU (
  input  in_1,
  input  CLK,
  input  in_3,
  input  [7:0] in_4,
  input  [3:0] intr3__0,
  output [15:0] ABUS,
  output [7:0] DOUTBUS,
  output inta,
  output [1:0] UEXT1__0,
  output out_10,
  output out_11
);

  wire Carry, ldIVTP;
  wire [1:0] grinst;
  wire [3:0] common_1_phaseffbus;
  wire [5:0] pull_resistor_3_node;
  wire [6:0] common_1_addrbus;
  wire [7:0] pull_resistor_6_node;
  wire [8:0] pull_resistor_8_node;
  wire [15:0] A, ALU, B, INTRADDR, PSW, pull_resistor_5_node;
  wire [19:0] pull_resistor_4_node;
  wire [20:0] common_1_instrucbus;

  COMMON common_1 (
    .CLK(CLK), .RST(in_1), .DIN(in_4), .CMEMBUS(pull_resistor_5_node), .MAR(ABUS), .MDR(DOUTBUS),
    .PHASEFFBUS(common_1_phaseffbus), .INSTRUCBUS(common_1_instrucbus), .ADDRBUS(common_1_addrbus),
    .PSW(PSW), .CREGBUS(pull_resistor_8_node), .CFFBUS(pull_resistor_6_node), .B(B), .A(A),
    .CPSW(pull_resistor_3_node), .ALU(ALU), .IVTPPDSP(INTRADDR), .CMEMBUS2(pull_resistor_4_node),
    .out_20(grinst), .in_12(Carry));  // open: out_21
  Pull_Resistor pull_resistor_1 (.node(common_1_instrucbus));
  Pull_Resistor pull_resistor_2 (.node(common_1_phaseffbus));
  Pull_Resistor pull_resistor_3 (.node(pull_resistor_3_node));
  Pull_Resistor pull_resistor_4 (.node(pull_resistor_4_node));
  Pull_Resistor pull_resistor_5 (.node(pull_resistor_5_node));
  Pull_Resistor pull_resistor_6 (.node(pull_resistor_6_node));
  Pull_Resistor pull_resistor_7 (.node(common_1_addrbus));
  Pull_Resistor pull_resistor_8 (.node(pull_resistor_8_node));
  FETCH fetch_1 (
    .in_3(in_1), .in_4(CLK), .in_1(in_3), .rdMEM(out_11), .INSTRUCBUS(common_1_instrucbus),
    .ADDRBUS(common_1_addrbus), .PHASEFFBUS(common_1_phaseffbus), .CMEMBUS(pull_resistor_5_node),
    .CFFBUS(pull_resistor_6_node), .CREGBUS(pull_resistor_8_node), .PSW(PSW), .in_2(grinst));
  ADDR addr_1 (
    .in_1(in_1), .in_2(CLK), .in_3(in_3), .CREGBUS(pull_resistor_8_node), .ADDRBUS(common_1_addrbus),
    .PHASEFFBUS(common_1_phaseffbus), .INSTRUCBUS(common_1_instrucbus), .CFFBUS(pull_resistor_6_node),
    .CMEMBUS(pull_resistor_5_node), .rdMEM(out_11));
  EXEC exec_1 (
    .in_2(in_1), .in_3(CLK), .in_4(in_3), .B(B), .A(A), .ALU(ALU), .CFFBUS(pull_resistor_6_node),
    .rdMEM(out_11), .wrMEM(out_10), .PHASEFFBUS(common_1_phaseffbus), .INSTRUCBUS(common_1_instrucbus),
    .ADDRBUS(common_1_addrbus), .PSW(PSW), .CPSW(pull_resistor_3_node), .CMEMBUS2(pull_resistor_4_node),
    .in_1(DOUTBUS), .Carry(Carry), .CMEMBUS(pull_resistor_5_node), .out_19(ldIVTP));
  INTR intr_1 (
    .in_1(in_1), .in_2(CLK), .in_3(in_3), .PHASEFFBUS(common_1_phaseffbus), .PSW(PSW), .intr(intr3__0),
    .ADDIVTP(INTRADDR), .CFFBUS(pull_resistor_6_node), .UEXT1__0(UEXT1__0), .inta(inta),
    .CREGBUS(pull_resistor_8_node), .CMEMBUS(pull_resistor_5_node), .CMEMBUS2(pull_resistor_4_node),
    .INSTRUCBUS(common_1_instrucbus), .in_5(ldIVTP), .rdMEM(out_11), .wrMEM(out_10), .A(A));

  // Other names for the same wires on the sheet: DIN7__0[7:0] = in_4; FCBUS = in_3; MAR[15:0] = ABUS;
  //   MDR[7:0] = DOUTBUS; RD = out_11; rst = in_1; WR = out_10
endmodule

module COMMON (
  input  CLK,
  input  RST,
  input  [7:0] DIN,
  input  [15:0] A,
  input  [15:0] ALU,
  input  [15:0] IVTPPDSP,
  input  [15:0] CMEMBUS,
  input  [19:0] CMEMBUS2,
  input  [7:0] CFFBUS,
  input  [8:0] CREGBUS,
  input  [5:0] CPSW,
  input  in_12,
  output [15:0] MAR,
  output [7:0] MDR,
  output [3:0] PHASEFFBUS,
  output [20:0] INSTRUCBUS,
  output [6:0] ADDRBUS,
  output [15:0] PSW,
  output [15:0] B,
  output [1:0] out_20,
  output [15:0] out_21
);

  wire adrinst, ainstrcillegal, and_1_out, and_3_out, and_8_out, and_9_out, and_10_out, and_11_out,
       and_13_out, and_14_out, and_15_out, and_16_out, and_17_out, and_18_out, and_19_out, and_20_out,
       and_21_out, and_22_out, and_23_out, and_24_out, and_25_out, and_26_out, and_27_out, and_28_out,
       and_29_out, and_30_out, and_31_out, and_32_out, AZERO, bezadrinst, branchinst, grinst1, grinst2,
       grinst3, grinst4, grinst5, instrcillegal, jmpinst, nor_1_out, nor_2_out, nor_3_out, nor_4_out,
       nor_5_out, nor_6_out, not_1_out, not_2_out, not_3_out, not_4_out, not_5_out, not_6_out, not_7_out,
       not_8_out, not_9_out, not_10_out, or_2_out, or_5_out, or_6_out, or_7_out, or_9_out, or_10_out,
       or_11_out, or_12_out, or_13_out, or_14_out, or_15_out, or_16_out, or_17_out, or_18_out, or_19_out,
       or_20_out, or_21_out, or_22_out, or_23_out, or_24_out, or_25_out, ujmpillegal;
  wire [2:0] IR27___24;
  wire [3:0] IR19__16;
  wire [7:0] IR7__0, IR15__8, mp2_8b_1_out_5, mp2_8b_2_out_5, mp2_8b_3_out_5, mp4_8b_1_y;
  wire [7:4] IR23__16, IR31__24;
  wire [15:0] add16_2_f, add16_3_f, ADDREL, GPR15__0, mp2_16b_1_out_5, mp4_16b_1_y, mp4_16b_2_y, mp4_16b_3_y,
       mp8_16b_1_y, mp8_16b_2_y, PC15__0, sub16_1_f;

  MP8_16b mp8_16b_1 (
    .En(1'b1), .S0(CMEMBUS[6]), .S1(CMEMBUS[9]), .S2(CMEMBUS2[10]), .I0(PC15__0), .I1({IR15__8, IR7__0}),
    .I2(GPR15__0), .I3(B), .I4(IVTPPDSP), .Y(mp8_16b_1_y));  // open: I5, I6, I7
  MP2_16b mp2_16b_1 (.En(1'b1), .in_2(mp8_16b_1_y), .in_3(out_21), .S0(CMEMBUS2[1]), .out_5(mp2_16b_1_out_5));
  REG16_INC_LD reg16_inc_ld_1 (
    .I15__0(mp2_16b_1_out_5), .LD(CMEMBUS[0]), .INC(CMEMBUS[1]), .CLK(CLK), .A15__0(MAR));  // open: mr
  or or_1 (instrcillegal, IR31__24[7], IR31__24[6]);
  REG8_LD reg8_ld_1 (
    .I7__0(MDR), .LD(CREGBUS[7]), .CLK(CLK), .A7__0({IR31__24, ainstrcillegal, IR27___24}));  // open: mr
  REG8_LD reg8_ld_2 (.I7__0(MDR), .LD(CREGBUS[5]), .CLK(CLK), .A7__0(IR15__8));  // open: mr
  DC2_4 dc2_4_1 (.En(PSW[0]), .X1__0(IR31__24[5:4]), .D0(bezadrinst), .D1(branchinst), .D2(jmpinst), .D3(adrinst));
  DC3_8 dc3_8_1 (
    .En(branchinst), .X2__0(IR27___24), .D0(INSTRUCBUS[8]), .D1(INSTRUCBUS[9]), .D2(INSTRUCBUS[10]),
    .D3(INSTRUCBUS[11]), .D4(INSTRUCBUS[12]));  // open: D5, D6, D7
  MP4_16b mp4_16b_1 (
    .En(1'b1), .S0(CMEMBUS[7]), .S1(CMEMBUS[8]), .I0({IR15__8, IR7__0}), .I1({MDR, B[7:0]}),
    .I2({B[15:8], MDR}), .I3(GPR15__0), .Y(mp4_16b_1_y));
  REG16_LD reg16_ld_1 (.I15__0(mp4_16b_1_y), .LD(CMEMBUS[5]), .CLK(CLK), .A15__0(B));  // open: mr
  ADD16 add16_1 (.C0(1'b0), .A(PC15__0), .B({{9{IR23__16[7]}}, IR23__16[6:4], IR19__16}), .F(ADDREL));  // open: C16
  and and_1 (and_1_out, INSTRUCBUS[16], ADDRBUS[0]);
  nor nor_1 (nor_1_out, INSTRUCBUS[8], INSTRUCBUS[9], INSTRUCBUS[10], INSTRUCBUS[11], INSTRUCBUS[12]);
  MP2_8b mp2_8b_1 (.in_2(PC15__0[15:8]), .in_3(PC15__0[7:0]), .S0(CMEMBUS[14]), .out_5(mp2_8b_1_out_5), .En(1'b1));
  nor nor_2 (nor_2_out, bezadrinst, branchinst, jmpinst, adrinst);
  nor nor_3 (nor_3_out, ADDRBUS[0], ADDRBUS[1], ADDRBUS[2], ADDRBUS[3], ADDRBUS[4], ADDRBUS[5], ADDRBUS[6]);
  and and_2 (grinst1, PSW[0], nor_2_out);
  and and_3 (and_3_out, adrinst, nor_3_out);
  and and_4 (grinst4, branchinst, or_2_out);
  or or_2 (or_2_out, nor_1_out, ainstrcillegal);
  MP4_8b mp4_8b_1 (
    .S0(CMEMBUS[12]), .S1(CMEMBUS[13]), .I0(DIN), .I1(mp2_8b_1_out_5), .I2(mp2_8b_2_out_5),
    .I3(mp2_8b_3_out_5), .Y(mp4_8b_1_y), .En(1'b1));
  REG8_LD reg8_ld_3 (.I7__0(mp4_8b_1_y), .LD(CMEMBUS[2]), .CLK(CLK), .A7__0(MDR));  // open: mr
  REG8_LD reg8_ld_4 (.I7__0(MDR), .LD(CREGBUS[6]), .CLK(CLK), .A7__0({IR23__16, IR19__16}));  // open: mr
  REG8_LD reg8_ld_5 (.I7__0(MDR), .LD(CREGBUS[4]), .CLK(CLK), .A7__0(IR7__0));  // open: mr
  or or_3 (ujmpillegal, ainstrcillegal, IR27___24[2]);
  SUB16 sub16_1 (.E0(1'b1), .A(out_21), .B({16{1'b0}}), .F(sub16_1_f));  // open: E16
  or or_4 (out_20[1], and_3_out, and_1_out);
  MP2_8b mp2_8b_2 (.in_2(A[15:8]), .in_3(A[7:0]), .S0(CMEMBUS[15]), .out_5(mp2_8b_2_out_5), .En(1'b1));
  DC4_16 dc4_16_1 (
    .En(bezadrinst), .X3__0({ainstrcillegal, IR27___24}), .D0(INSTRUCBUS[0]), .D1(INSTRUCBUS[1]),
    .D2(INSTRUCBUS[2]), .D3(INSTRUCBUS[3]), .D4(INSTRUCBUS[4]), .D5(INSTRUCBUS[5]), .D6(INSTRUCBUS[6]),
    .D7(INSTRUCBUS[7]));  // open: D8, D9, D10, D11, D12, D13, D14, D15
  DC2_4 dc2_4_2 (.En(jmpinst), .X1__0(IR27___24[1:0]), .D0(INSTRUCBUS[13]), .D1(INSTRUCBUS[14]));  // open: D2, D3
  MP4_16b mp4_16b_2 (
    .En(1'b1), .S0(CMEMBUS2[7]), .S1(CMEMBUS2[8]), .I0(16'hf000), .I1(sub16_1_f), .I2(MAR), .Y(mp4_16b_2_y));  // open: I3
  REG16_INC_LD reg16_inc_ld_2 (
    .I15__0(mp4_16b_2_y), .LD(or_5_out), .INC(CMEMBUS2[9]), .CLK(CLK), .A15__0(out_21));  // open: mr
  MP2_8b mp2_8b_3 (
    .in_2({PSW[15], {7{1'b0}}}), .in_3({3'b000, PSW[4:0]}), .S0(CMEMBUS2[0]), .out_5(mp2_8b_3_out_5),
    .En(1'b1));
  or or_5 (or_5_out, RST, CMEMBUS2[6]);
  nor nor_4 (nor_4_out, INSTRUCBUS[0], INSTRUCBUS[1], INSTRUCBUS[2], INSTRUCBUS[3], INSTRUCBUS[4], INSTRUCBUS[5], INSTRUCBUS[6], INSTRUCBUS[7]);
  nor nor_5 (nor_5_out, INSTRUCBUS[15], INSTRUCBUS[16], INSTRUCBUS[17], INSTRUCBUS[18], INSTRUCBUS[19], INSTRUCBUS[20]);
  nor nor_6 (nor_6_out, INSTRUCBUS[13], INSTRUCBUS[14]);
  DC3_8 dc3_8_2 (
    .En(adrinst), .X2__0(IR27___24), .D0(INSTRUCBUS[15]), .D1(INSTRUCBUS[16]), .D2(INSTRUCBUS[17]),
    .D3(INSTRUCBUS[18]), .D4(INSTRUCBUS[19]), .D5(INSTRUCBUS[20]));  // open: D6, D7
  ADD16 add16_2 (.C0(1'b0), .A(GPR15__0), .B(16'hfffe), .F(add16_2_f));  // open: C16
  and and_5 (grinst2, bezadrinst, nor_4_out);
  or or_6 (or_6_out, nor_5_out, instrcillegal);
  and and_6 (grinst5, jmpinst, or_7_out);
  or or_7 (or_7_out, nor_6_out, ujmpillegal);
  not not_1 (not_1_out, RST);
  RSFF rsff_1 (.S(CFFBUS[0]), .CLK(CLK), .R(CFFBUS[1]), .Sd(not_1_out), .Q(PHASEFFBUS[0]));  // open: Rd, notQ
  MP8_16b mp8_16b_2 (
    .En(1'b1), .S0(CMEMBUS2[3]), .S1(CMEMBUS2[4]), .S2(CMEMBUS2[5]), .I0(16'h1000),
    .I1({IR23__16, IR19__16, IR15__8}), .I2({MDR, PC15__0[7:0]}), .I3({PC15__0[15:8], MDR}), .I4(ADDREL),
    .Y(mp8_16b_2_y));  // open: I5, I6, I7
  REG16_INC_LD reg16_inc_ld_3 (
    .I15__0(mp8_16b_2_y), .LD(or_9_out), .INC(CMEMBUS[4]), .CLK(CLK), .A15__0(PC15__0));  // open: mr
  DC3_8 dc3_8_3 (
    .En(adrinst), .X2__0(IR23__16[6:4]), .D0(ADDRBUS[0]), .D1(ADDRBUS[1]), .D2(ADDRBUS[2]), .D3(ADDRBUS[3]),
    .D4(ADDRBUS[4]), .D5(ADDRBUS[5]), .D6(ADDRBUS[6]));  // open: D7
  MP4_16b mp4_16b_3 (
    .En(1'b1), .S0(CMEMBUS[11]), .S1(CMEMBUS2[2]), .I0(add16_2_f), .I1(add16_3_f), .I2(A), .Y(mp4_16b_3_y));  // open: I3
  GPR16x16 gpr16x16_1 (.DI15__0(mp4_16b_3_y), .A3__0(IR19__16), .WR(CMEMBUS[10]), .CLK(CLK), .DO15__0(GPR15__0));
  and and_7 (grinst3, adrinst, or_6_out);
  or or_8 (out_20[0], grinst1, grinst2, grinst3, grinst4, grinst5, instrcillegal);
  or or_9 (or_9_out, CMEMBUS[3], RST);
  ADD16 add16_3 (.C0(1'b0), .A(GPR15__0), .B(16'h2), .F(add16_3_f));  // open: C16
  RSFF rsff_2 (.S(CFFBUS[2]), .CLK(CLK), .R(CFFBUS[3]), .Rd(not_2_out), .Q(PHASEFFBUS[1]));  // open: Sd, notQ
  not not_2 (not_2_out, RST);
  or or_10 (or_10_out, INSTRUCBUS[2], INSTRUCBUS[6]);
  or or_11 (or_11_out, INSTRUCBUS[2], INSTRUCBUS[6]);
  or or_12 (or_12_out, INSTRUCBUS[2], INSTRUCBUS[6]);
  or or_13 (or_13_out, INSTRUCBUS[15], INSTRUCBUS[17], INSTRUCBUS[18], INSTRUCBUS[19], INSTRUCBUS[20], INSTRUCBUS[3], INSTRUCBUS[4]);
  or or_14 (or_14_out, INSTRUCBUS[15], INSTRUCBUS[17], INSTRUCBUS[18], INSTRUCBUS[19], INSTRUCBUS[20], INSTRUCBUS[3], INSTRUCBUS[4]);
  or or_15 (or_15_out, INSTRUCBUS[2], INSTRUCBUS[6]);
  and and_8 (and_8_out, ~ALU[15], A[15], B[15]);  // AND_Gate
  or or_16 (or_16_out, and_8_out, and_9_out);
  and and_9 (and_9_out, ALU[15], ~A[15], ~B[15]);  // AND_Gate
  or or_17 (or_17_out, INSTRUCBUS[2], INSTRUCBUS[6]);
  or or_18 (or_18_out, INSTRUCBUS[17], INSTRUCBUS[18], INSTRUCBUS[3], INSTRUCBUS[4]);
  RSFF rsff_3 (.S(CFFBUS[4]), .CLK(CLK), .R(CFFBUS[5]), .Rd(not_3_out), .Q(PHASEFFBUS[2]));  // open: Sd, notQ
  not not_3 (not_3_out, RST);
  and and_10 (and_10_out, or_10_out, MDR[1]);
  and and_11 (and_11_out, or_13_out, AZERO);
  and and_12 (AZERO, ~A[0], ~A[1], ~A[2], ~A[3], ~A[4], ~A[5], ~A[6], ~A[7], ~A[8], ~A[9], ~A[10], ~A[11], ~A[12], ~A[13], ~A[14], ~A[15]);  // AND_Gate
  and and_13 (and_13_out, or_11_out, MDR[2]);
  and and_14 (and_14_out, or_14_out, A[15]);
  and and_15 (and_15_out, or_15_out, MDR[3]);
  and and_16 (and_16_out, INSTRUCBUS[18], AZERO);
  and and_17 (and_17_out, INSTRUCBUS[17], or_16_out);
  and and_18 (and_18_out, or_17_out, MDR[4]);
  and and_19 (and_19_out, or_18_out, in_12);
  or or_19 (or_19_out, INSTRUCBUS[2], INSTRUCBUS[6]);
  and and_20 (and_20_out, ~MDR[0], or_12_out, CPSW[5]);  // AND_Gate
  and and_21 (and_21_out, MDR[0], or_12_out, CPSW[5]);
  or or_20 (or_20_out, and_10_out, and_11_out);
  or or_21 (or_21_out, and_13_out, and_14_out);
  or or_22 (or_22_out, and_15_out, or_23_out);
  or or_23 (or_23_out, and_16_out, and_17_out);
  or or_24 (or_24_out, and_18_out, and_19_out);
  and and_22 (and_22_out, or_19_out, MDR[7]);
  or or_25 (or_25_out, and_20_out, CPSW[0]);
  and and_23 (and_23_out, ~or_21_out, CPSW[1]);  // AND_Gate
  and and_24 (and_24_out, CPSW[1], or_21_out);
  RSFF rsff_4 (.S(CFFBUS[6]), .CLK(CLK), .R(CFFBUS[7]), .Rd(not_4_out), .Q(PHASEFFBUS[3]));  // open: Sd, notQ
  not not_4 (not_4_out, RST);
  not not_5 (not_5_out, RST);
  RSFF rsff_5 (.S(and_21_out), .CLK(CLK), .R(or_25_out), .Sd(not_5_out), .Q(PSW[0]));  // open: Rd, notQ
  and and_25 (and_25_out, ~or_20_out, CPSW[1]);  // AND_Gate
  RSFF rsff_6 (.S(and_26_out), .CLK(CLK), .R(and_25_out), .Rd(not_6_out), .Q(PSW[1]));  // open: Sd, notQ
  not not_6 (not_6_out, RST);
  and and_26 (and_26_out, CPSW[1], or_20_out);
  RSFF rsff_7 (.S(and_24_out), .CLK(CLK), .R(and_23_out), .Rd(not_7_out), .Q(PSW[2]));  // open: Sd, notQ
  not not_7 (not_7_out, RST);
  and and_27 (and_27_out, ~or_22_out, CPSW[2]);  // AND_Gate
  and and_28 (and_28_out, CPSW[2], or_22_out);
  and and_29 (and_29_out, ~or_24_out, CPSW[3]);  // AND_Gate
  and and_30 (and_30_out, CPSW[3], or_24_out);
  and and_31 (and_31_out, ~and_22_out, CPSW[4]);  // AND_Gate
  RSFF rsff_8 (.S(and_32_out), .CLK(CLK), .R(and_31_out), .Sd(not_10_out), .Q(PSW[15]));  // open: Rd, notQ
  and and_32 (and_32_out, CPSW[4], and_22_out);
  RSFF rsff_9 (.S(and_28_out), .CLK(CLK), .R(and_27_out), .Rd(not_8_out), .Q(PSW[3]));  // open: Sd, notQ
  not not_8 (not_8_out, RST);
  RSFF rsff_10 (.S(and_30_out), .CLK(CLK), .R(and_29_out), .Rd(not_9_out), .Q(PSW[4]));  // open: Sd, notQ
  not not_9 (not_9_out, RST);
  not not_10 (not_10_out, RST);

  assign PSW[14:5] = {10{1'b0}};

  // Other names for the same wires on the sheet: B15__0[15:0] = B; IR23__16[3:0] = IR19__16; MDR7__0[7:0] = MDR;
  //   A15__0[15:0] = A; immed = ADDRBUS[0]; memdir = ADDRBUS[1]; memind = ADDRBUS[2]; regind = ADDRBUS[3];
  //   preincr = ADDRBUS[4]; postdec = ADDRBUS[5]; regdir = ADDRBUS[6]; ALU15__0[15:0] = ALU; Carry = in_12;
  //   stFETCH = CFFBUS[0]; clFETCH = CFFBUS[1]; stADDR = CFFBUS[2]; clADDR = CFFBUS[3]; stEXEC = CFFBUS[4];
  //   clEXEC = CFFBUS[5]; stINTR = CFFBUS[6]; clINTR = CFFBUS[7]; ldMAR = CMEMBUS[0]; incMAR = CMEMBUS[1];
  //   ldMDR = CMEMBUS[2]; ldPC = CMEMBUS[3]; incPC = CMEMBUS[4]; ldB = CMEMBUS[5]; mxMAR0 = CMEMBUS[6];
  //   mxB0 = CMEMBUS[7]; mxB1 = CMEMBUS[8]; mxMAR1 = CMEMBUS[9]; wrGPR = CMEMBUS[10]; mxGPR0 = CMEMBUS[11];
  //   mxMDR0 = CMEMBUS[12]; mxMDR1 = CMEMBUS[13]; mxMDRPC = CMEMBUS[14]; mxMDRA = CMEMBUS[15]; mxMPSW = CMEMBUS2[0];
  //   mxMARSP = CMEMBUS2[1]; mxGPR1 = CMEMBUS2[2]; mxPC0 = CMEMBUS2[3]; mxPC1 = CMEMBUS2[4]; mxPC2 = CMEMBUS2[5];
  //   decSP = CMEMBUS2[6]; mxSP0 = CMEMBUS2[7]; mxSP1 = CMEMBUS2[8]; incSP = CMEMBUS2[9]; mxMAR2 = CMEMBUS2[10];
  //   clPSWSTART = CPSW[0]; ldZ_ldN = CPSW[1]; ldV = CPSW[2]; ldC = CPSW[3]; ldI = CPSW[4]; ldSTART = CPSW[5];
  //   ldIR7__0 = CREGBUS[4]; ldIR15__8 = CREGBUS[5]; ldIR23__16 = CREGBUS[6]; ldIR31__24 = CREGBUS[7];
  //   Din7__0[7:0] = DIN; ENTRADDR15__0[15:0] = IVTPPDSP; HALT = INSTRUCBUS[0]; RTS = INSTRUCBUS[1];
  //   RTI = INSTRUCBUS[2]; ROR = INSTRUCBUS[3]; RORC = INSTRUCBUS[4]; PUSHPSW = INSTRUCBUS[5]; POPPSW = INSTRUCBUS[6];
  //   STIVTP = INSTRUCBUS[7]; BGREU = INSTRUCBUS[8]; BLSSU = INSTRUCBUS[9]; BLEQU = INSTRUCBUS[10];
  //   JGRT = INSTRUCBUS[11]; JLEQ = INSTRUCBUS[12]; JMP = INSTRUCBUS[13]; JSR = INSTRUCBUS[14]; LD = INSTRUCBUS[15];
  //   ST = INSTRUCBUS[16]; ADD = INSTRUCBUS[17]; DEC = INSTRUCBUS[18]; OR = INSTRUCBUS[19]; STRFIND = INSTRUCBUS[20];
  //   IR31__24[3:0] = {ainstrcillegal, IR27___24}; cjmpillegal = ainstrcillegal; IR27___24[3] = ainstrcillegal;
  //   MAR15__0[15:0] = MAR; grinst1b = out_20[0]; grinst2b = out_20[1]; FETCH = PHASEFFBUS[0]; ADDR = PHASEFFBUS[1];
  //   EXEC = PHASEFFBUS[2]; INTR = PHASEFFBUS[3]; PSWSTART = PSW[0]; PSWZ = PSW[1]; PSWN = PSW[2]; PSWV = PSW[3];
  //   PSWC = PSW[4]; PSWI = PSW[15]; SP15__0[15:0] = out_21

  // Notes on the sheet:
  //   MAR
  //   Pomocni registar
  //   Instrukcijski registar
  //   Dekoderi za prepoznavanje instrukcije na osnovu sadrzaja registra IR23..16
  //   Stack Pointer
  //   MDR
  //   PC
  //   Registarski fajl
  //   FF za pokretanje FETCH, ADDR, EXEC i INTR faze izvršavanja instrukcije
  //   Programska statusna reč (PSW)
endmodule

module FETCH (
  input  in_1,
  input  [1:0] in_2,
  input  in_3,
  input  in_4,
  input  [3:0] PHASEFFBUS,
  input  [20:0] INSTRUCBUS,
  input  [6:0] ADDRBUS,
  input  [15:0] PSW,
  output [15:0] CMEMBUS,
  output [7:0] CFFBUS,
  output [8:0] CREGBUS,
  output rdMEM
);

  wire addr2, addr4, addr_t, and_3_out, and_4_out, and_5_out, and_6_out, and_7_out, and_8_out, and_9_out,
       and_10_out, bezadr1, bradr2, brbezadr1, brcnd, brgrinst1b, brgrinst2b, brjmp2, brjmp3, brnotfcmem,
       bruncnd, clFETCH, incPC, jmp2, jmp3, ldIR7__0, ldIR15__8, ldIR23__16, ldIR31__24, ldMAR, ldMDR,
       not_1_out, not_2_out, not_3_out, not_4_out, not_5_out, notPSWSTandFETCH, or_4_out, or_5_out, or_6_out,
       or_7_out, or_9_out, rdMEM_t, stADDR, stEXEC;
  wire [3:0] rom_32x24_1_dout;
  wire [4:0] reg8_inc_ld_1_a7__0, rom_32x24_1_dout_3;
  wire [7:5] reg8_inc_ld_1_a7__0_2, undriven;
  wire [23:11] rom_32x24_1_dout_2;

  not not_1 (not_1_out, in_3);
  or or_1 (jmp2, INSTRUCBUS[8], INSTRUCBUS[9], INSTRUCBUS[10]);
  or or_2 (jmp3, INSTRUCBUS[11], INSTRUCBUS[12], INSTRUCBUS[13], INSTRUCBUS[14]);
  REG8_INC_LD reg8_inc_ld_1 (
    .I7__0({undriven, rom_32x24_1_dout_3}), .LD(or_4_out), .INC(not_2_out), .mr(not_1_out), .CLK(in_4),
    .A7__0({reg8_inc_ld_1_a7__0_2, reg8_inc_ld_1_a7__0}));
  not not_2 (not_2_out, or_4_out);
  ROM_32x24 rom_32x24_1 (
    .A4__0(reg8_inc_ld_1_a7__0), .CS(1'b1),
    .DOUT({rom_32x24_1_dout_2[23:21], rom_32x24_1_dout_3, rom_32x24_1_dout, rom_32x24_1_dout_2[11], stEXEC, stADDR, clFETCH, ldIR7__0, ldIR15__8, ldIR23__16, ldIR31__24, ldMDR, rdMEM_t, incPC, ldMAR}));
  DC4_16 dc4_16_1 (
    .En(1'b1), .X3__0(rom_32x24_1_dout), .D1(bruncnd), .D2(notPSWSTandFETCH), .D3(brbezadr1), .D4(brjmp2),
    .D5(bradr2), .D6(brjmp3), .D7(brnotfcmem), .D8(brgrinst1b), .D9(brgrinst2b));  // open: D0, D10, D11, D12, D13, D14, D15
  or or_3 (bezadr1, INSTRUCBUS[0], INSTRUCBUS[1], INSTRUCBUS[2], INSTRUCBUS[3], INSTRUCBUS[4], INSTRUCBUS[5], INSTRUCBUS[6], INSTRUCBUS[7]);
  or or_4 (or_4_out, bruncnd, brcnd);
  not not_3 (not_3_out, PHASEFFBUS[0]);
  not not_4 (not_4_out, PSW[0]);
  or or_5 (or_5_out, ADDRBUS[3], ADDRBUS[4], ADDRBUS[5], ADDRBUS[6]);
  or or_6 (or_6_out, ADDRBUS[0], ADDRBUS[1], ADDRBUS[2]);
  or or_7 (or_7_out, not_3_out, not_4_out);
  or or_8 (addr_t, INSTRUCBUS[15], INSTRUCBUS[16], INSTRUCBUS[17], INSTRUCBUS[18], INSTRUCBUS[19], INSTRUCBUS[20]);
  and and_1 (addr2, or_5_out, addr_t);
  and and_2 (addr4, addr_t, or_6_out);
  not not_5 (not_5_out, in_1);
  and and_3 (and_3_out, in_2[0], brgrinst1b);
  and and_4 (and_4_out, in_2[1], brgrinst2b);
  and and_5 (and_5_out, or_7_out, notPSWSTandFETCH);
  and and_6 (and_6_out, brbezadr1, bezadr1);
  and and_7 (and_7_out, brjmp2, jmp2);
  and and_8 (and_8_out, bradr2, addr2);
  and and_9 (and_9_out, brjmp3, jmp3);
  and and_10 (and_10_out, brnotfcmem, not_5_out);
  or or_9 (or_9_out, and_3_out, and_4_out);
  or or_10 (brcnd, and_5_out, and_6_out, and_7_out, and_8_out, and_9_out, and_10_out, or_9_out);
  assign CMEMBUS[2] = ldMDR ? 1'b1 : 1'bz;  // Controlled_Buffer controlled_buffer_1
  assign CMEMBUS[4] = incPC ? 1'b1 : 1'bz;  // Controlled_Buffer controlled_buffer_2
  assign CMEMBUS[0] = ldMAR ? 1'b1 : 1'bz;  // Controlled_Buffer controlled_buffer_3
  assign CREGBUS[4] = ldIR7__0 ? 1'b1 : 1'bz;  // Controlled_Buffer controlled_buffer_4
  assign CREGBUS[5] = ldIR15__8 ? 1'b1 : 1'bz;  // Controlled_Buffer controlled_buffer_5
  assign CREGBUS[6] = ldIR23__16 ? 1'b1 : 1'bz;  // Controlled_Buffer controlled_buffer_6
  assign CREGBUS[7] = ldIR31__24 ? 1'b1 : 1'bz;  // Controlled_Buffer controlled_buffer_7
  assign rdMEM = rdMEM_t ? 1'b1 : 1'bz;  // Controlled_Buffer controlled_buffer_8
  assign CFFBUS[1] = clFETCH ? 1'b1 : 1'bz;  // Controlled_Buffer controlled_buffer_9
  assign CFFBUS[2] = stADDR ? 1'b1 : 1'bz;  // Controlled_Buffer controlled_buffer_10
  assign CFFBUS[4] = stEXEC ? 1'b1 : 1'bz;  // Controlled_Buffer controlled_buffer_11

  // Other names for the same wires on the sheet: immed = ADDRBUS[0]; memdir = ADDRBUS[1]; memind = ADDRBUS[2];
  //   regind = ADDRBUS[3]; preincr = ADDRBUS[4]; postdec = ADDRBUS[5]; regdir = ADDRBUS[6]; stFETCH = CFFBUS[0];
  //   clADDR = CFFBUS[3]; clEXEC = CFFBUS[5]; stINTR = CFFBUS[6]; clINTR = CFFBUS[7]; CLK = in_4; FCBUS = in_1;
  //   grinst1b = in_2[0]; grinst2b = in_2[1]; HALT = INSTRUCBUS[0]; RTS = INSTRUCBUS[1]; RTI = INSTRUCBUS[2];
  //   ROR = INSTRUCBUS[3]; RORC = INSTRUCBUS[4]; PUSHPSW = INSTRUCBUS[5]; POPPSW = INSTRUCBUS[6];
  //   STIVTP = INSTRUCBUS[7]; BGREU = INSTRUCBUS[8]; BLSSU = INSTRUCBUS[9]; BLEQU = INSTRUCBUS[10];
  //   JGRT = INSTRUCBUS[11]; JLEQ = INSTRUCBUS[12]; JMP = INSTRUCBUS[13]; JSR = INSTRUCBUS[14]; LD = INSTRUCBUS[15];
  //   ST = INSTRUCBUS[16]; ADD = INSTRUCBUS[17]; DEC = INSTRUCBUS[18]; OR = INSTRUCBUS[19]; STRFIND = INSTRUCBUS[20];
  //   FETCH = PHASEFFBUS[0]; ADDR = PHASEFFBUS[1]; EXEC = PHASEFFBUS[2]; INTR = PHASEFFBUS[3]; PSW15__0[15:0] = PSW;
  //   PSWSTART = PSW[0]; rst = in_3

  // Notes on the sheet:
  //   Operaciona jedinica
  //   Kontrolna jedinica
endmodule

module ADDR (
  input  in_1,
  input  in_2,
  input  in_3,
  input  [3:0] PHASEFFBUS,
  input  [6:0] ADDRBUS,
  input  [20:0] INSTRUCBUS,
  output [15:0] CMEMBUS,
  output [7:0] CFFBUS,
  output [8:0] CREGBUS,
  output rdMEM
);

  wire and_1_out, and_2_out, and_3_out, braddr, brcnd, brnotADDR, brnotFCBUS, brSTORE, bruncnd,
       clADDR_stEXEC, incMAR, ldB, ldMAR, ldMDR, mxB0, mxB1, mxGRP0, mxMAR0, mxMAR1, not_1_out, not_2_out,
       not_3_out, not_4_out, or_1_out, rdMEM_t, wrGPR;
  wire [2:0] rom_32x24_addr_1_dout_2;
  wire [3:0] kmadraddr_1_adr3__0;
  wire [4:0] reg8_inc_ld_1_a7__0, rom_32x24_addr_1_dout;
  wire [7:0] mp2_8b_1_out_5;
  wire [7:5] reg8_inc_ld_1_a7__0_2;
  wire [23:15] rom_32x24_addr_1_dout_3;

  not not_1 (not_1_out, in_1);
  KMADRADDR kmadraddr_1 (
    .immed(ADDRBUS[0]), .memdir(ADDRBUS[1]), .memind(ADDRBUS[2]), .regind(ADDRBUS[3]), .preincr(ADDRBUS[4]),
    .postdecr(ADDRBUS[5]), .regdir(ADDRBUS[6]), .Adr3__0(kmadraddr_1_adr3__0));
  MP2_8b mp2_8b_1 (
    .in_2({3'b000, rom_32x24_addr_1_dout}), .in_3({4'b0000, kmadraddr_1_adr3__0}), .S0(braddr),
    .out_5(mp2_8b_1_out_5), .En(1'b1));
  REG8_INC_LD reg8_inc_ld_1 (
    .I7__0(mp2_8b_1_out_5), .LD(or_1_out), .INC(not_2_out), .mr(not_1_out), .CLK(in_2),
    .A7__0({reg8_inc_ld_1_a7__0_2, reg8_inc_ld_1_a7__0}));
  ROM_32x24_addr rom_32x24_addr_1 (
    .A4__0(reg8_inc_ld_1_a7__0), .CS(1'b1),
    .DOUT({rom_32x24_addr_1_dout_3[23:21], rom_32x24_addr_1_dout, rom_32x24_addr_1_dout_3[15], rom_32x24_addr_1_dout_2, clADDR_stEXEC, mxGRP0, wrGPR, mxMAR1, mxB1, mxB0, incMAR, mxMAR0, ldMDR, rdMEM_t, ldB, ldMAR}));
  or or_1 (or_1_out, bruncnd, braddr, brcnd);
  not not_2 (not_2_out, or_1_out);
  DC3_8 dc3_8_1 (
    .En(1'b1), .X2__0(rom_32x24_addr_1_dout_2), .D1(bruncnd), .D2(brnotADDR), .D3(brSTORE), .D4(brnotFCBUS),
    .D5(braddr));  // open: D0, D6, D7
  not not_3 (not_3_out, PHASEFFBUS[1]);
  not not_4 (not_4_out, in_3);
  and and_1 (and_1_out, not_3_out, brnotADDR);
  and and_2 (and_2_out, brSTORE, INSTRUCBUS[16]);
  and and_3 (and_3_out, brnotFCBUS, not_4_out);
  or or_2 (brcnd, and_1_out, and_2_out, and_3_out);
  assign rdMEM = rdMEM_t ? 1'b1 : 1'bz;  // Controlled_Buffer controlled_buffer_1
  assign CMEMBUS[0] = ldMAR ? 1'b1 : 1'bz;  // Controlled_Buffer controlled_buffer_2
  assign CMEMBUS[1] = incMAR ? 1'b1 : 1'bz;  // Controlled_Buffer controlled_buffer_3
  assign CMEMBUS[2] = ldMDR ? 1'b1 : 1'bz;  // Controlled_Buffer controlled_buffer_4
  assign CMEMBUS[5] = ldB ? 1'b1 : 1'bz;  // Controlled_Buffer controlled_buffer_5
  assign CMEMBUS[6] = mxMAR0 ? 1'b1 : 1'bz;  // Controlled_Buffer controlled_buffer_6
  assign CMEMBUS[7] = mxB0 ? 1'b1 : 1'bz;  // Controlled_Buffer controlled_buffer_7
  assign CMEMBUS[8] = mxB1 ? 1'b1 : 1'bz;  // Controlled_Buffer controlled_buffer_8
  assign CMEMBUS[9] = mxMAR1 ? 1'b1 : 1'bz;  // Controlled_Buffer controlled_buffer_9
  assign CMEMBUS[10] = wrGPR ? 1'b1 : 1'bz;  // Controlled_Buffer controlled_buffer_10
  assign CMEMBUS[11] = mxGRP0 ? 1'b1 : 1'bz;  // Controlled_Buffer controlled_buffer_11
  assign CFFBUS[3] = clADDR_stEXEC ? 1'b1 : 1'bz;  // Controlled_Buffer controlled_buffer_12
  assign CFFBUS[4] = clADDR_stEXEC ? 1'b1 : 1'bz;  // Controlled_Buffer controlled_buffer_13

  // Other names for the same wires on the sheet: immed = ADDRBUS[0]; memdir = ADDRBUS[1]; memind = ADDRBUS[2];
  //   regind = ADDRBUS[3]; preincr = ADDRBUS[4]; postdec = ADDRBUS[5]; regdir = ADDRBUS[6]; CLK = in_2; FCBUS = in_3;
  //   ST = INSTRUCBUS[16]; FETCH = PHASEFFBUS[0]; ADDR = PHASEFFBUS[1]; EXEC = PHASEFFBUS[2]; INTR = PHASEFFBUS[3];
  //   rst = in_1

  // Notes on the sheet:
  //   Operaciona jedinica
  //   Upravljacka jedinica
endmodule

module EXEC (
  input  [7:0] in_1,
  input  in_2,
  input  in_3,
  input  in_4,
  input  [15:0] B,
  input  [3:0] PHASEFFBUS,
  input  [20:0] INSTRUCBUS,
  input  [6:0] ADDRBUS,
  input  [15:0] PSW,
  output [15:0] A,
  output [15:0] ALU,
  output [15:0] CMEMBUS,
  output [19:0] CMEMBUS2,
  output [7:0] CFFBUS,
  output [5:0] CPSW,
  output rdMEM,
  output wrMEM,
  output Carry,
  output out_19
);

  wire and_2_out, and_3_out, and_4_out, and_5_out, and_6_out, and_7_out, and_8_out, and_10_out, and_11_out,
       and_12_out, and_13_out, and_14_out, BRANCH, brcnd, brMDRZERO, brnotbrorjmp, brnoteq, brnotEXEC,
       brnotFCBUS, bropr, brorjmp, brregdir, bruncnd, CarryAlu, clCOUNT, decSP, incCOUNT, incMAR, incSP,
       JAPS, ldA, ldMAR, ldMDR, ldN, ldPC, MDRZERO, mxA0, mxA1, mxA2, mxADD, mxALU, mxGPR1, mxMAR0, mxMAR1,
       mxMARSP, mxMDR0, mxMDR1, mxMDRA, mxMDRPC, mxMPSW, mxPC0, mxPC1, mxPC2, mxROR_RORC, mxSP0, mxSP1,
       not_1_out, not_2_out, not_3_out, not_4_out, not_5_out, not_6_out, not_7_out, noteq, or_4_out,
       or_8_out, or_9_out, rdMEM_t, stINTR_clEXEC, tres, wrGPR, wrMEM_t, xor_1_out;
  wire [3:0] rom256x52_1_dout59__28_2;
  wire [7:0] kmdar_exec_1_adr7__0, mp2_8b_1_out_5, reg8_inc_ld_1_a7__0, rom256x52_1_dout59__28_3, sub8_1_f;
  wire [15:0] COUNT15__0, mp2_16b_1_out_5, mp2_16b_2_out_5, mp2_16b_3_out_5, mp8_16b_1_y, or_3_out;
  wire [15:15] RORA;
  wire [19:12] rom256x52_1_dout59__28;

  MP2_1b mp2_1b_1 (.I0(A[0]), .I1(PSW[4]), .S0(mxROR_RORC), .Y(RORA[15]), .En(1'b1));
  or or_1 (BRANCH, INSTRUCBUS[10], INSTRUCBUS[8], INSTRUCBUS[9]);
  or or_2 (JAPS, INSTRUCBUS[12], INSTRUCBUS[11]);
  not not_1 (not_1_out, in_2);
  assign or_3_out = A | B;  // OR_Gate or_3, 16 bits wide
  KMDAR_EXEC kmdar_exec_1 (
    .LD(INSTRUCBUS[15]), .ST(INSTRUCBUS[16]), .ADD(INSTRUCBUS[17]), .DEC(INSTRUCBUS[18]),
    .OR(INSTRUCBUS[19]), .STRFIND(INSTRUCBUS[20]), .BRANCH(BRANCH), .JAPS(JAPS), .JMP(INSTRUCBUS[13]),
    .JSR(INSTRUCBUS[14]), .RTS(INSTRUCBUS[1]), .RTI(INSTRUCBUS[2]), .ROR(INSTRUCBUS[3]),
    .RORC(INSTRUCBUS[4]), .PUSHPSW(INSTRUCBUS[5]), .POPPSW(INSTRUCBUS[6]), .STIVTP(INSTRUCBUS[7]),
    .HALT(INSTRUCBUS[0]), .Adr7__0(kmdar_exec_1_adr7__0));
  MP2_8b mp2_8b_1 (
    .in_2(rom256x52_1_dout59__28_3), .in_3(kmdar_exec_1_adr7__0), .S0(bropr), .out_5(mp2_8b_1_out_5),
    .En(1'b1));
  REG8_INC_LD reg8_inc_ld_1 (
    .I7__0(mp2_8b_1_out_5), .LD(or_4_out), .INC(not_2_out), .mr(not_1_out), .CLK(in_3),
    .A7__0(reg8_inc_ld_1_a7__0));
  MP8_16b mp8_16b_1 (
    .En(1'b1), .S0(mxA0), .S1(mxA1), .S2(mxA2), .I0(B), .I1(ALU), .I2(or_3_out), .I3({RORA[15], A[15:1]}),
    .I4(COUNT15__0), .I5({16{1'b1}}), .Y(mp8_16b_1_y));  // open: I6, I7
  REG16_CL_LD reg16_cl_ld_1 (.I15__0(mp8_16b_1_y), .CL(in_2), .LD(ldA), .CLK(in_3), .A15__0(A));  // open: mr
  or or_4 (or_4_out, bruncnd, bropr, brcnd);
  not not_2 (not_2_out, or_4_out);
  ROM256x52 rom256x52_1 (
    .A7__0(reg8_inc_ld_1_a7__0), .CS(1'b1),
    .DOUT59__28({rom256x52_1_dout59__28_3, rom256x52_1_dout59__28_2, rom256x52_1_dout59__28, mxROR_RORC, stINTR_clEXEC, CPSW[0], out_19, CPSW[5:4], incSP, mxSP1, mxSP0, decSP, mxPC2, mxPC1}),
    .DOUT27__0({mxPC0, ldPC, incCOUNT, clCOUNT, mxALU, mxGPR1, wrGPR, mxMARSP, mxMAR1, mxMAR0, ldMAR, incMAR, wrMEM_t, rdMEM_t, mxMPSW, mxMDRA, mxMDRPC, mxMDR1, mxMDR0, ldMDR, CPSW[2], CPSW[3], CPSW[1], ldN, mxA2, mxA1, mxA0, ldA}));
  DC4_16 dc4_16_1 (
    .En(1'b1), .X3__0(rom256x52_1_dout59__28_2), .D1(bruncnd), .D2(brnotEXEC), .D3(brregdir),
    .D4(brnotbrorjmp), .D5(brnotFCBUS), .D6(brMDRZERO), .D7(bropr), .D8(brnoteq));  // open: D0, D9, D10, D11, D12, D13, D14, D15
  or or_5 (Carry, A[0], CarryAlu);
  MP2_16b mp2_16b_1 (.En(1'b1), .in_2(A), .in_3(B), .S0(mxALU), .out_5(mp2_16b_1_out_5));
  and and_1 (MDRZERO, ~in_1[0], ~in_1[1], ~in_1[2], ~in_1[3], ~in_1[4], ~in_1[5], ~in_1[6], ~in_1[7]);  // AND_Gate
  MP2_16b mp2_16b_2 (.En(1'b1), .in_2(COUNT15__0), .in_3({16{1'b1}}), .S0(mxALU), .out_5(mp2_16b_2_out_5));
  MP2_16b mp2_16b_3 (.En(1'b1), .in_2(mp2_16b_2_out_5), .in_3(B), .S0(mxADD), .out_5(mp2_16b_3_out_5));
  ADD16 add16_1 (.C0(1'b0), .A(mp2_16b_1_out_5), .B(mp2_16b_3_out_5), .F(ALU), .C16(CarryAlu));
  not not_3 (not_3_out, PHASEFFBUS[2]);
  not not_4 (not_4_out, brorjmp);
  not not_5 (not_5_out, in_4);
  REG16_INC_LD reg16_inc_ld_1 (
    .I15__0({16{1'b0}}), .LD(clCOUNT), .INC(incCOUNT), .CLK(in_3), .A15__0(COUNT15__0));  // open: mr
  and and_2 (and_2_out, not_3_out, brnotEXEC);
  and and_3 (and_3_out, brregdir, ADDRBUS[6]);
  and and_4 (and_4_out, brnotbrorjmp, not_4_out);
  and and_5 (and_5_out, noteq, brnoteq);
  and and_6 (and_6_out, MDRZERO, brMDRZERO);
  and and_7 (and_7_out, not_5_out, brnotFCBUS);
  and and_8 (and_8_out, ~mxA2, ~mxA1, mxA0);  // AND_Gate
  SUB8 sub8_1 (.E0(1'b0), .A(in_1), .B(A[7:0]), .F(sub8_1_f), .E8(tres));
  or or_6 (noteq, sub8_1_f[7], sub8_1_f[6], sub8_1_f[5], sub8_1_f[4], sub8_1_f[3], sub8_1_f[2], sub8_1_f[1], sub8_1_f[0]);
  or or_7 (brcnd, and_2_out, and_3_out, and_4_out, and_5_out, and_6_out, and_7_out);
  and and_9 (mxADD, and_8_out, INSTRUCBUS[17]);
  not not_6 (not_6_out, PSW[4]);
  or or_8 (or_8_out, PSW[1], PSW[4]);
  or or_9 (or_9_out, PSW[1], xor_1_out);
  xor xor_1 (xor_1_out, PSW[2], PSW[3]);
  not not_7 (not_7_out, or_9_out);
  and and_10 (and_10_out, not_6_out, INSTRUCBUS[8]);
  and and_11 (and_11_out, or_8_out, INSTRUCBUS[10]);
  and and_12 (and_12_out, PSW[4], INSTRUCBUS[9]);
  and and_13 (and_13_out, not_7_out, INSTRUCBUS[11]);
  and and_14 (and_14_out, or_9_out, INSTRUCBUS[12]);
  or or_10 (brorjmp, and_10_out, and_11_out, and_12_out, and_13_out, and_14_out);
  // ROM_EXEC rom_exec_1: pin names not known
  assign CMEMBUS2[0] = mxMPSW ? 1'b1 : 1'bz;  // Controlled_Buffer controlled_buffer_1
  assign CMEMBUS2[1] = mxMARSP ? 1'b1 : 1'bz;  // Controlled_Buffer controlled_buffer_2
  assign CMEMBUS2[2] = mxGPR1 ? 1'b1 : 1'bz;  // Controlled_Buffer controlled_buffer_3
  assign CMEMBUS2[3] = mxPC0 ? 1'b1 : 1'bz;  // Controlled_Buffer controlled_buffer_4
  assign CMEMBUS2[4] = mxPC1 ? 1'b1 : 1'bz;  // Controlled_Buffer controlled_buffer_5
  assign CMEMBUS2[5] = mxPC2 ? 1'b1 : 1'bz;  // Controlled_Buffer controlled_buffer_6
  assign CMEMBUS2[6] = decSP ? 1'b1 : 1'bz;  // Controlled_Buffer controlled_buffer_7
  assign CMEMBUS2[7] = mxSP0 ? 1'b1 : 1'bz;  // Controlled_Buffer controlled_buffer_8
  assign CMEMBUS2[8] = mxSP1 ? 1'b1 : 1'bz;  // Controlled_Buffer controlled_buffer_9
  assign CMEMBUS2[9] = incSP ? 1'b1 : 1'bz;  // Controlled_Buffer controlled_buffer_10
  assign CMEMBUS[0] = ldMAR ? 1'b1 : 1'bz;  // Controlled_Buffer controlled_buffer_11
  assign CMEMBUS[1] = incMAR ? 1'b1 : 1'bz;  // Controlled_Buffer controlled_buffer_12
  assign CMEMBUS[2] = ldMDR ? 1'b1 : 1'bz;  // Controlled_Buffer controlled_buffer_13
  assign CMEMBUS[3] = ldPC ? 1'b1 : 1'bz;  // Controlled_Buffer controlled_buffer_14
  assign CMEMBUS[6] = mxMAR0 ? 1'b1 : 1'bz;  // Controlled_Buffer controlled_buffer_15
  assign CMEMBUS[9] = mxMAR1 ? 1'b1 : 1'bz;  // Controlled_Buffer controlled_buffer_16
  assign CMEMBUS[10] = wrGPR ? 1'b1 : 1'bz;  // Controlled_Buffer controlled_buffer_17
  assign CMEMBUS[12] = mxMDR0 ? 1'b1 : 1'bz;  // Controlled_Buffer controlled_buffer_18
  assign CMEMBUS[13] = mxMDR1 ? 1'b1 : 1'bz;  // Controlled_Buffer controlled_buffer_19
  assign CMEMBUS[14] = mxMDRPC ? 1'b1 : 1'bz;  // Controlled_Buffer controlled_buffer_20
  assign CMEMBUS[15] = mxMDRA ? 1'b1 : 1'bz;  // Controlled_Buffer controlled_buffer_21
  assign CFFBUS[5] = stINTR_clEXEC ? 1'b1 : 1'bz;  // Controlled_Buffer controlled_buffer_22
  assign CFFBUS[6] = stINTR_clEXEC ? 1'b1 : 1'bz;  // Controlled_Buffer controlled_buffer_23
  assign rdMEM = rdMEM_t ? 1'b1 : 1'bz;  // Controlled_Buffer controlled_buffer_24
  assign wrMEM = wrMEM_t ? 1'b1 : 1'bz;  // Controlled_Buffer controlled_buffer_25

  // Other names for the same wires on the sheet: ldIVTP = out_19; A7__0[7:0] = A[7:0]; A15__0[15:0] = A;
  //   CarryRor = A[0]; RORA[14:0] = A[15:1]; regdir = ADDRBUS[6]; ALU15__0[15:0] = ALU; B15__0[15:0] = B; CLK = in_3;
  //   clPSWSTART = CPSW[0]; ldZ = CPSW[1]; ldV = CPSW[2]; ldC = CPSW[3]; ldI = CPSW[4]; ldSTART = CPSW[5];
  //   FCBUS = in_4; HALT = INSTRUCBUS[0]; RTS = INSTRUCBUS[1]; RTI = INSTRUCBUS[2]; ROR = INSTRUCBUS[3];
  //   RORC = INSTRUCBUS[4]; PUSHPSW = INSTRUCBUS[5]; POPPSW = INSTRUCBUS[6]; STIVTP = INSTRUCBUS[7];
  //   BGREU = INSTRUCBUS[8]; BLSSU = INSTRUCBUS[9]; BLEQU = INSTRUCBUS[10]; JGRT = INSTRUCBUS[11];
  //   JLEQ = INSTRUCBUS[12]; JMP = INSTRUCBUS[13]; JSR = INSTRUCBUS[14]; LD = INSTRUCBUS[15]; ST = INSTRUCBUS[16];
  //   ADD = INSTRUCBUS[17]; DEC = INSTRUCBUS[18]; OR = INSTRUCBUS[19]; STRFIND = INSTRUCBUS[20]; MDR7__0[7:0] = in_1;
  //   FETCH = PHASEFFBUS[0]; ADDR = PHASEFFBUS[1]; EXEC = PHASEFFBUS[2]; INTR = PHASEFFBUS[3]; PSWSTART = PSW[0];
  //   PSWZ = PSW[1]; PSWN = PSW[2]; PSWV = PSW[3]; PSWC = PSW[4]; PSWI = PSW[15]; rst = in_2

  // Notes on the sheet:
  //   Amburator
  //   Operaciona jedinica
  //   Upravljacka jedinica
endmodule

module INTR (
  input  in_1,
  input  in_2,
  input  in_3,
  input  [3:0] PHASEFFBUS,
  input  in_5,
  input  [15:0] A,
  input  [15:0] PSW,
  input  [3:0] intr,
  input  [20:0] INSTRUCBUS,
  output [15:0] ADDIVTP,
  output [1:0] UEXT1__0,
  output inta,
  output [15:0] CMEMBUS,
  output [19:0] CMEMBUS2,
  output [7:0] CFFBUS,
  output [8:0] CREGBUS,
  output rdMEM,
  output wrMEM
);

  wire and_2_out, and_3_out, and_4_out, and_5_out, brcnd, brnotFCBUS, brnotINTR, brnotprekid, bruncnd, decSP,
       incMAR, ldMAR, ldMDR, ldPC, mxMARSP, mxMDR0, mxMDR1, mxMDRPC, mxMPSW, mxPC0, mxPC1, mxSP0, not_1_out,
       not_2_out, not_3_out, not_4_out, not_5_out, not_6_out, not_7_out, or_2_out, prekid, prper, rdMEM_t,
       stFETCH_clINTR, wrMEM_t;
  wire [2:0] rom32x26_1_dout;
  wire [2:1] IVTDSP15__0;
  wire [4:0] reg8_inc_ld_1_a7__0, rom32x26_1_dout_2;
  wire [7:5] reg8_inc_ld_1_a7__0_2, undriven;
  wire [15:0] IVTP15__0;

  not not_1 (not_1_out, in_1);
  and and_1 (prekid, prper, PSW[15], not_3_out);
  REG16_LD reg16_ld_1 (.I15__0(A), .LD(in_5), .CLK(in_2), .A15__0(IVTP15__0), .mr(not_1_out));
  not not_2 (not_2_out, in_1);
  REG8_INC_LD reg8_inc_ld_1 (
    .I7__0({undriven, rom32x26_1_dout_2}), .LD(or_2_out), .INC(not_4_out), .mr(not_2_out), .CLK(in_2),
    .A7__0({reg8_inc_ld_1_a7__0_2, reg8_inc_ld_1_a7__0}));
  not not_3 (not_3_out, INSTRUCBUS[0]);
  not not_4 (not_4_out, or_2_out);
  ROM32x26 rom32x26_1 (
    .A3__0(reg8_inc_ld_1_a7__0), .CS(1'b1),
    .DOUT({rom32x26_1_dout_2, rom32x26_1_dout, stFETCH_clINTR, inta, mxSP0, decSP, rdMEM_t, wrMEM_t, mxMDRPC, mxMPSW, mxMDR1, mxMDR0, ldMDR, CMEMBUS2[10], mxMARSP, incMAR, ldMAR, mxPC1, mxPC0, ldPC}));
  DC3_8 dc3_8_1 (
    .En(1'b1), .X2__0(rom32x26_1_dout), .D1(bruncnd), .D2(brnotINTR), .D3(brnotprekid), .D4(brnotFCBUS));  // open: D0, D5, D6, D7
  or or_1 (prper, intr[3], intr[2], intr[1], intr[0]);
  or or_2 (or_2_out, bruncnd, brcnd);
  CD4 cd4_1 (
    .C3(intr[3]), .C2(intr[2]), .C1(intr[1]), .C0(intr[0]), .Z1(UEXT1__0[1]), .Z0(UEXT1__0[0]), .En(1'b1));  // open: W
  REG2_LD reg2_ld_1 (.LD(inta), .CLK(in_2), .I1__0(UEXT1__0), .A1__0(IVTDSP15__0));  // open: mr
  not not_5 (not_5_out, PHASEFFBUS[3]);
  not not_6 (not_6_out, prekid);
  not not_7 (not_7_out, in_3);
  and and_2 (and_2_out, not_5_out, brnotINTR);
  and and_3 (and_3_out, not_6_out, brnotprekid);
  and and_4 (and_4_out, not_7_out, brnotFCBUS);
  or or_3 (brcnd, and_2_out, and_3_out, and_4_out);
  ADD16 add16_1 (.C0(1'b0), .A(IVTP15__0), .B({{13{1'b0}}, IVTDSP15__0, 1'b0}), .F(ADDIVTP));  // open: C16
  assign CMEMBUS2[0] = mxMPSW ? 1'b1 : 1'bz;  // Controlled_Buffer controlled_buffer_1
  assign CMEMBUS2[1] = mxMARSP ? 1'b1 : 1'bz;  // Controlled_Buffer controlled_buffer_2
  assign CMEMBUS2[3] = mxPC0 ? 1'b1 : 1'bz;  // Controlled_Buffer controlled_buffer_3
  assign CMEMBUS2[4] = mxPC1 ? 1'b1 : 1'bz;  // Controlled_Buffer controlled_buffer_4
  assign CMEMBUS2[6] = decSP ? 1'b1 : 1'bz;  // Controlled_Buffer controlled_buffer_5
  assign CMEMBUS2[7] = mxSP0 ? 1'b1 : 1'bz;  // Controlled_Buffer controlled_buffer_6
  assign CMEMBUS[0] = ldMAR ? 1'b1 : 1'bz;  // Controlled_Buffer controlled_buffer_7
  assign CMEMBUS[1] = incMAR ? 1'b1 : 1'bz;  // Controlled_Buffer controlled_buffer_8
  assign CMEMBUS[2] = ldMDR ? 1'b1 : 1'bz;  // Controlled_Buffer controlled_buffer_9
  assign CMEMBUS[3] = ldPC ? 1'b1 : 1'bz;  // Controlled_Buffer controlled_buffer_10
  assign CMEMBUS[12] = mxMDR0 ? 1'b1 : 1'bz;  // Controlled_Buffer controlled_buffer_11
  assign CMEMBUS[13] = mxMDR1 ? 1'b1 : 1'bz;  // Controlled_Buffer controlled_buffer_12
  assign CMEMBUS[14] = mxMDRPC ? 1'b1 : 1'bz;  // Controlled_Buffer controlled_buffer_13
  assign rdMEM = rdMEM_t ? 1'b1 : 1'bz;  // Controlled_Buffer controlled_buffer_14
  assign wrMEM = wrMEM_t ? 1'b1 : 1'bz;  // Controlled_Buffer controlled_buffer_15
  and and_5 (and_5_out, PSW[0], stFETCH_clINTR);
  assign CFFBUS[0] = and_5_out ? 1'b1 : 1'bz;  // Controlled_Buffer controlled_buffer_16
  assign CFFBUS[7] = stFETCH_clINTR ? 1'b1 : 1'bz;  // Controlled_Buffer controlled_buffer_17

  // Other names for the same wires on the sheet: ldBR = inta; A15__0[15:0] = A; ADDIVTP15__0[15:0] = ADDIVTP;
  //   CLK = in_2; mxMAR2 = CMEMBUS2[10]; FCBUS = in_3; HALT = INSTRUCBUS[0]; RTS = INSTRUCBUS[1]; RTI = INSTRUCBUS[2];
  //   ROR = INSTRUCBUS[3]; RORC = INSTRUCBUS[4]; PUSHPSW = INSTRUCBUS[5]; POPPSW = INSTRUCBUS[6];
  //   STIVTP = INSTRUCBUS[7]; BGREU = INSTRUCBUS[8]; BLSSU = INSTRUCBUS[9]; BLEQU = INSTRUCBUS[10];
  //   JGRT = INSTRUCBUS[11]; JLEQ = INSTRUCBUS[12]; JMP = INSTRUCBUS[13]; JSR = INSTRUCBUS[14]; LD = INSTRUCBUS[15];
  //   ST = INSTRUCBUS[16]; ADD = INSTRUCBUS[17]; DEC = INSTRUCBUS[18]; OR = INSTRUCBUS[19]; STRFIND = INSTRUCBUS[20];
  //   intr3__0[3:0] = intr; ldIVTP = in_5; FETCH = PHASEFFBUS[0]; ADDR = PHASEFFBUS[1]; EXEC = PHASEFFBUS[2];
  //   INTR_t = PHASEFFBUS[3]; PSWSTART = PSW[0]; PSWI = PSW[15]; rst = in_1

  // Notes on the sheet:
  //   Operaciona jedinica
  //   Upravljacka jedinica
endmodule

module RAM (
  input  [15:0] in_1,
  input  in_2,
  input  [7:0] in_3,
  input  in_4,
  input  in_5,
  input  in_6,
  output [7:0] out_7,
  output out_8
);

  wire and_1_out, and_2_out, CNT0, LDCNT, not_1_out, not_2_out, not_3_out, notCNT0, or_1_out, rsff_2_q, sl,
       xor_1_out;
  wire [3:0] CNT, LFSR;

  RSFF rsff_1 (.S(in_6), .CLK(in_2), .R(1'b0), .Q(sl));  // open: Sd, Rd, notQ
  or or_1 (or_1_out, in_4, in_5);
  REG4_LD_SL_SR reg4_ld_sl_sr_1 (
    .I3__0(4'b1111), .LD(in_6), .IR(1'b0), .SR(1'b0), .IL(xor_1_out), .SL(sl), .CLK(in_2), .A3__0(LFSR));  // open: mr
  RisingEdge risingedge_1 (.INPUT(or_1_out), .CLK(in_2), .OUTPUT(LDCNT));
  MEM64Kx8 mem64kx8_1 (.WR_RD(in_4), .A15__0(in_1), .DIN(in_3), .CS(1'b1), .CLK(in_2), .DOUT(out_7));
  xor xor_1 (xor_1_out, LFSR[2], LFSR[3]);
  and and_1 (and_1_out, CNT0, not_1_out);
  not not_1 (not_1_out, LDCNT);
  RSFF rsff_2 (.S(LDCNT), .CLK(in_2), .R(and_1_out), .Rd(not_2_out), .Q(rsff_2_q));  // open: Sd, notQ
  not not_2 (not_2_out, in_6);
  and and_2 (and_2_out, rsff_2_q, CNT0);
  REG4m_DEC_LD reg4m_dec_ld_1 (
    .I3__0(LFSR), .LD(LDCNT), .Ein(notCNT0), .DEC(notCNT0), .CLK(in_2), .A3__0(CNT));  // open: Eout, mr
  or or_2 (notCNT0, CNT[0], CNT[1], CNT[2], CNT[3]);
  RSFF rsff_3 (.S(and_2_out), .CLK(in_2), .R(out_8), .Rd(not_3_out), .Q(out_8));  // open: Sd, notQ
  not not_3 (not_3_out, in_6);
  not not_4 (CNT0, notCNT0);

  // Other names for the same wires on the sheet: ADR[15:0] = in_1; CLK = in_2; DIN[7:0] = in_3; DOUT[7:0] = out_7;
  //   fc = out_8; RDMEM = in_5; rst = in_6; WRMEM = in_4

  // Notes on the sheet:
  //   Random broj predstavlja vreme pristupa memoriji
  //   Brojac za generisanje random broja 
  //   Jedinica za generisanje function complete (fc) signala
  //   Brojac za dekrementiranje random broja
endmodule
